# Fritzing sketch lab3 (saved by Fritzing 0.9.6b)
breadboards: 2

parts:
  Mod1 = Raspberry Pi 4B
  LED1 = LED - 5mm [color="Red (635nm)" current=0.030 package="5 mm [THT]"]
  LED2 = LED - 5mm [color="Yellow (595nm)" current=0.030 package="5 mm [THT]"]
  LED3 = LED - 5mm [color="Green (565nm)" current=0.030 package="5 mm [THT]"]
  R1 = Resistor [tolerance=±5% resistance=220 package="0805 [SMD]"]
  R2 = Resistor [tolerance=±5% resistance=220 package="0805 [SMD]"]
  R3 = Resistor [tolerance=±5% resistance=220 package="0805 [SMD]"]

nets:
  N1: Mod1.GND, R1.Pin_1, R2.Pin_0, R3.Pin_0
  N2: Mod1.GPIO14, LED1.anode
  N3: Mod1.GPIO7, LED2.anode
  N4: Mod1.GPIO12, LED3.anode
  N5: LED1.cathode, R1.Pin_0
  N6: LED2.cathode, R2.Pin_1
  N7: LED3.cathode, R3.Pin_1
